// Logisim project Processor.circ as structural Verilog: 1 circuit, main circuit main
module main (
);

  wire and_1_out, and_2_out, and_3_out, and_4_out, and_6_out, and_11_out, and_12_out, and_14_out, CLK,
       comparator_1_eq, comparator_2_eq, comparator_3_eq, comparator_4_eq, comparator_5_eq, comparator_6_eq,
       comparator_7_eq, comparator_8_eq, comparator_9_eq, comparator_10_eq, comparator_11_eq, control_1_p2,
       control_1_p3, control_1_p4, control_1_p5, control_1_p6, control_1_p7, datamem_1_p1, exmem_1_p10,
       exmem_1_p11, exmem_1_p13, exmem_1_p14, exmem_1_p15, exmem_1_p16, idex_1_p7, idex_1_p11, idex_1_p12,
       idex_1_p13, idex_1_p15, idex_1_p18, ifid_1_p7, ifid_1_p8, memwb_1_p7, nor_1_out, not_1_out, not_2_out,
       operand_1_p4, or_1_out, or_2_out, or_3_out, or_4_out, or_5_out, pcfile_1_p2, pcfile_1_p8, reg_1_p5,
       reg_1_p8, Stall, Taken;
  wire [1:0] and_7_out, and_8_out, and_9_out, control_1_p8, control_1_p9, idex_1_p14, memwb_1_p6, pcfile_1_p5;
  wire [3:0] exmem_1_p12, idex_1_p10, idex_1_p16, idex_1_p17, multiplexer_2_out, pcfile_1_p1_3, reg_1_p4;
  wire [7:0] exmem_1_p9_2;
  wire [11:0] pcfile_1_p1;
  wire [23:0] bit_extender_1_out, Branch, exmem_1_p9, idex_1_p8, idex_1_p9, memwb_1_p3, pcfile_1_p7;
  wire [31:0] alu_1_p1, bit_extender_2_out, exmem_1_p3, idex_1_p4, idex_1_p5, idex_1_p6, idex_1_p19,
       idex_1_p20, memwb_1_p1, memwb_1_p2, multiplexer_1_out, reg_1_p6, rom_1_data;
  wire [31:12] pcfile_1_p1_2;

  Clock clock_1 (.out(CLK));
  not not_1 (not_1_out, Stall);
  // PCfile pcfile_1: pin names not known; wires that end beside it: {pcfile_1_p1_2[31:24], pcfile_1_p1_3, pcfile_1_p1_2[19:12], pcfile_1_p1}, pcfile_1_p2, CLK, Branch, pcfile_1_p5, not_1_out, pcfile_1_p7, pcfile_1_p8
  ROM #(.addrWidth(24), .dataWidth(32)) rom_1 (.addr(pcfile_1_p7), .data(rom_1_data));
  or or_1 (or_1_out, control_1_p9[1], Taken);
  Multiplexer #(.width(32)) multiplexer_1 (.in0(rom_1_data), .in1({32{1'b0}}), .out(multiplexer_1_out), .sel(or_1_out));
  not not_2 (not_2_out, Stall);
  // IFID ifid_1: pin names not known; wires that end beside it: CLK, multiplexer_1_out, pcfile_1_p7, pcfile_1_p8, not_2_out, {pcfile_1_p1_2[31:24], pcfile_1_p1_3, pcfile_1_p1_2[19:12], pcfile_1_p1}, ifid_1_p7, ifid_1_p8
  // Control control_1: pin names not known; wires that end beside it: pcfile_1_p1_2[31:24], control_1_p2, control_1_p3, control_1_p4, control_1_p5, control_1_p6, control_1_p7, control_1_p8, control_1_p9
  Multiplexer #(.width(4)) multiplexer_2 (
    .in0(pcfile_1_p1_3), .in1(4'b1111), .out(multiplexer_2_out), .sel(control_1_p6));
  assign bit_extender_1_out = {{12{pcfile_1_p1[11]}}, pcfile_1_p1};  // Bit_Extender bit_extender_1
  Multiplexer #(.width(2)) multiplexer_3 (.in0(control_1_p9), .in1(2'b01), .out(pcfile_1_p5), .sel(Taken));
  Comparator comparator_1 (.a(8'h40), .b(pcfile_1_p1_2[31:24]), .eq(comparator_1_eq));  // open: gt, lt
  // Reg reg_1: pin names not known; wires that end beside it: pcfile_1_p1_2[19:16], pcfile_1_p1_2[15:12], CLK, reg_1_p4, reg_1_p5, reg_1_p6, pcfile_1_p2, reg_1_p8
  nor nor_1 (nor_1_out, control_1_p8[0], control_1_p8[1]);
  Comparator #(.width(4)) comparator_2 (.a(exmem_1_p12), .b(4'b0000), .eq(comparator_2_eq));  // open: gt, lt
  or or_2 (or_2_out, Stall, Taken);
  // Operand operand_1: pin names not known; wires that end beside it: {pcfile_1_p1_2[31:24], pcfile_1_p1_3, pcfile_1_p1_2[19:12], pcfile_1_p1}, reg_1_p8, control_1_p8, operand_1_p4, multiplexer_2_out, control_1_p4, control_1_p5, control_1_p2, control_1_p7, control_1_p3, pcfile_1_p1_2[19:16], pcfile_1_p1_2[15:12], nor_1_out
  or or_3 (or_3_out, nor_1_out, control_1_p4);
  Comparator #(.width(4)) comparator_3 (
    .a(exmem_1_p12), .b(pcfile_1_p1_2[19:16]), .eq(comparator_3_eq));  // open: gt, lt
  and and_1 (and_1_out, or_3_out, comparator_5_eq);
  // IDEX idex_1: pin names not known; wires that end beside it: CLK, or_2_out, pcfile_1_p2, idex_1_p4, idex_1_p5, idex_1_p6, idex_1_p7, idex_1_p8, idex_1_p9, idex_1_p10, idex_1_p11, idex_1_p12, idex_1_p13, idex_1_p14, idex_1_p15, idex_1_p16, idex_1_p17, idex_1_p18, idex_1_p19, idex_1_p20, idex_1_p15
  or or_4 (or_4_out, and_1_out, comparator_4_eq);
  Comparator #(.width(4)) comparator_4 (
    .a(idex_1_p10), .b(pcfile_1_p1_2[19:16]), .eq(comparator_4_eq));  // open: gt, lt
  Comparator #(.width(4)) comparator_5 (
    .a(idex_1_p10), .b(pcfile_1_p1_2[15:12]), .eq(comparator_5_eq));  // open: gt, lt
  and and_2 (and_2_out, exmem_1_p14, comparator_3_eq, comparator_2_eq);
  Comparator #(.width(2)) comparator_6 (.a(idex_1_p14), .b(2'b01), .eq(comparator_6_eq));  // open: gt, lt
  Comparator #(.width(4)) comparator_7 (.a(idex_1_p10), .b(4'b0000), .eq(comparator_7_eq));  // open: gt, lt
  // ALU alu_1: pin names not known; wires that end beside it: alu_1_p1
  and and_3 (and_3_out, comparator_7_eq, idex_1_p12, comparator_4_eq);
  and and_4 (and_4_out, or_4_out, ~comparator_7_eq, idex_1_p12, comparator_6_eq);  // AND_Gate
  and and_5 (Taken, idex_1_p13, alu_1_p1[0]);
  or or_5 (or_5_out, and_3_out, and_2_out);
  Adder #(.width(24)) adder_1 (.a(idex_1_p8), .b(idex_1_p9), .out(Branch));  // open: cin, cout
  and and_6 (and_6_out, ~Taken, or_5_out, comparator_1_eq);  // AND_Gate
  or or_6 (Stall, and_4_out, and_6_out);
  // EXMEM exmem_1: pin names not known; wires that end beside it: CLK, alu_1_p1, exmem_1_p3, idex_1_p7, idex_1_p10, idex_1_p11, idex_1_p12, idex_1_p14, {exmem_1_p9_2, exmem_1_p9}, exmem_1_p10, exmem_1_p11, exmem_1_p12, exmem_1_p13, exmem_1_p14, exmem_1_p15, exmem_1_p16, exmem_1_p9, exmem_1_p13, CLK, exmem_1_p10
  Comparator #(.width(4)) comparator_8 (.a(exmem_1_p12), .b(idex_1_p16), .eq(comparator_8_eq));  // open: gt, lt
  and and_7 (and_7_out[0], comparator_8_eq, exmem_1_p16, exmem_1_p14);
  Multiplexer #(.select(2), .width(32)) multiplexer_4 (
    .in0(idex_1_p4), .in1({exmem_1_p9_2, exmem_1_p9}), .in2(reg_1_p6), .out(idex_1_p19), .sel(and_7_out));  // open: in3
  Comparator #(.width(4)) comparator_9 (.a(exmem_1_p12), .b(idex_1_p17), .eq(comparator_9_eq));  // open: gt, lt
  // DataMem datamem_1: pin names not known; wires that end beside it: datamem_1_p1, CLK, {exmem_1_p9_2, exmem_1_p9}, datamem_1_p1, exmem_1_p11, exmem_1_p12, exmem_1_p14, exmem_1_p15
  and and_8 (and_8_out[0], comparator_9_eq, exmem_1_p16, exmem_1_p14, idex_1_p18);
  Multiplexer #(.select(2), .width(32)) multiplexer_5 (
    .in0(idex_1_p5), .in1({exmem_1_p9_2, exmem_1_p9}), .in2(reg_1_p6), .out(idex_1_p20), .sel(and_8_out));  // open: in3
  and and_9 (and_9_out[0], comparator_9_eq, exmem_1_p16, exmem_1_p14);
  and and_10 (and_9_out[1], and_11_out, ~and_9_out[0]);  // AND_Gate
  Multiplexer #(.select(2), .width(32)) multiplexer_6 (
    .in0(idex_1_p6), .in1({exmem_1_p9_2, exmem_1_p9}), .in2(reg_1_p6), .out(exmem_1_p3), .sel(and_9_out));  // open: in3
  and and_11 (and_11_out, memwb_1_p7, reg_1_p5, comparator_10_eq);
  // MEMWB memwb_1: pin names not known; wires that end beside it: memwb_1_p1, memwb_1_p2, memwb_1_p3, reg_1_p4, reg_1_p5, memwb_1_p6, memwb_1_p7
  assign bit_extender_2_out = {{8{1'b0}}, memwb_1_p3};  // Bit_Extender bit_extender_2
  Comparator #(.width(4)) comparator_10 (.a(reg_1_p4), .b(idex_1_p17), .eq(comparator_10_eq));  // open: gt, lt
  Comparator #(.width(4)) comparator_11 (.a(reg_1_p4), .b(idex_1_p16), .eq(comparator_11_eq));  // open: gt, lt
  and and_12 (and_12_out, comparator_11_eq, memwb_1_p7, reg_1_p5);
  and and_13 (and_7_out[1], and_12_out, ~and_7_out[0]);  // AND_Gate
  Multiplexer #(.select(2), .width(32)) multiplexer_7 (
    .in0(memwb_1_p1), .in1(memwb_1_p2), .in2(bit_extender_2_out), .in3({32{1'b0}}), .out(reg_1_p6),
    .sel(memwb_1_p6));
  and and_14 (and_14_out, comparator_10_eq, memwb_1_p7, reg_1_p5, idex_1_p18);
  and and_15 (and_8_out[1], and_14_out, ~and_8_out[0]);  // AND_Gate

  // Notes on the sheet:
  //   contents of rom_1 (hex, n*v repeats v):
  //   50100007 5020fffd 50d00001 312000 50400004 31034096 50d00002 1312000 5040000a 31034092 50d00003
  //   2321000 50400001 3103408e 50d00004 3321000 50400000 3103408a 50d00005 4312000 50400005 31034086
  //   50d00006 5312000 5040ffff 31034082 50d00007 6312000 5040fffa 3103407e 50d00008 7312000 50400000
  //   3103407a 50d00009 5031fff6 5040fffd 31034076 50d0000a 52320000 50400001 31034072 50d0000b 5331ffff
  //   50400001 3103406e 50d0000c 5432ffff 5540fffd 3103406a 50d0000d 55318000 55408007 31034066 50d0000e
  //   5632ffff 5c40ffff 55440002 31034061 50d0000f 58310004 50400070 3103405d 50d00010 5932001c 5040000f
  //   31034059 50d00011 5a320001 5040fffe 31034055 50d00012 5b310001 5c408000 55440003 31034050 50d00013
  //   5c301234 50401234 58440010 3103404b 50d00014 50000005 300000 50400000 31034046 50d00015 50500003
  //   355000 50400006 31034041 50d00016 50500004 50600001 355000 50400008 3103403b 50d00017 50500002
  //   50600009 356000 5040000b 31034035 50d00018 50500001 50500014 350000 50400014 3103402f 50d00019
  //   5050004d 20005064 10600064 366000 5040009a 31034028 50d0001a 50500062 10350002 5040004d 31034023
  //   50d0001b 10600064 20006065 10300065 5040004d 3103401d 50d0001c 3001201b 50d0001d 50300005 31012003
  //   50300063 50300063 50400005 31034014 50d0001e 50500007 30051002 6000009b 3100000f 50d0001f 60000090
  //   6000009b 50300000 50d00020 6100009e 5040002a 31034007 503f0000 50400093 31034004 50e0600d 2000e000
  //   6000009a 50e00bad 2000e000 6000009d 5030002a 400f0000
  //   IF
  //   ID
  //   Hazard Detection
  //   EX
  //   MEM
  //   Forwarding
  //   WB
endmodule
